# Fritzing sketch fp_lock_wiring_diagram (saved by Fritzing 0.9.3b)

parts:
  Part1 = Arduino Uno (Rev3)
  LCD1 = LCD screen
  S1 = Pushbutton [package="[THT]"]
  S2 = Pushbutton [package="[THT]"]
  S3 = Pushbutton [package="[THT]"]
  S4 = Pushbutton [package="[THT]"]
  U1 = RF-LINK_TX [package=rf-link_tx]
  J1 = Basic Servo
  R3 = Resistor [tolerance=±5% resistance=220 package=THT]
  R4 = Resistor [tolerance=±5% resistance=220 package=THT]
  R5 = Resistor [tolerance=±5% resistance=220 package=THT]
  R6 = Resistor [tolerance=±5% resistance=220 package=THT]
  R7 = Resistor [tolerance=±5% resistance=220 package=THT]  # not connected

nets:
  N1: Part1.A2, R6.Pin_1
  N2: Part1.A3, R4.Pin_1
  N3: Part1.A4/SDA, R3.Pin_1
  N4: Part1.A5/SCL, R5.Pin_1
  N5: Part1.D9_PWM, J1.pulse
  N6: Part1.D11_PWM/MOSI, LCD1.E
  N7: Part1.D12/MISO, LCD1.RS
  N8: Part1.D2, LCD1.DB7
  N9: Part1.D3_PWM, LCD1.DB6
  N10: Part1.D4, LCD1.DB5
  N11: Part1.D5_PWM, LCD1.DB4
  N12: Part1.D6_PWM, U1.DATA
  N13: Part1.D7, U1.+5V
  5V: Part1.5V, J1.vcc
  GND: Part1.GND, U1.GND, J1.gnd
  N14: S1.Pin_2, R5.Pin_0
  N15: S2.Pin_1, S2.Pin_2, R3.Pin_0
  N16: S3.Pin_1, S3.Pin_2, R4.Pin_0
  N17: S4.Pin_1, S4.Pin_2, R6.Pin_0
